// Logisim project labdarbas.circ as structural Verilog
module ALU (
  input  [7:0] in_1,
  input  [7:0] X,
  input  [7:0] Y,
  output [7:0] Z,
  output ZF,
  output BAF,
  output BOF
);

  wire [7:0] add_1_z, and_1_z, dec_1_out_2, div_1_z, inc_1_out_2, inv_1_z, mul_1_z, n0_1_out_2, n1_1_out_2,
       neg_1_out_2, not_1_z, op1_1_out_3, op2_1_out_3, op3_1_z, or_1_z, rol_1_z, ror_1_z, shl_1_z, shr_1_z,
       sub_1_z, vld_1_z, xor_1_z;
  wire [9:8] cmpz_1_zf;
  wire [10:8] add_1_zf, and_1_zf, dec_1_zf, div_1_zf, inc_1_zf, inv_1_zf, mul_1_baf, n0_1_zf, n1_1_zf,
       neg_1_baf, not_1_zf, op1_1_zf, op2_1_zf, op3_1_zf, or_1_zf, rol_1_zf, ror_1_zf, shl_1_zf, shr_1_zf,
       sub_1_zf, vld_1_zf, xor_1_zf;

  VLD vld_1 (.X(X), .Z(vld_1_z), .ZF(vld_1_zf[8]), .BAF(vld_1_zf[9]), .BOF(vld_1_zf[10]));
  NEG neg_1 (.X(X), .out_2(neg_1_out_2), .BAF(neg_1_baf[8]), .ZF(neg_1_baf[9]), .BOF(neg_1_baf[10]));
  INC inc_1 (.X(X), .out_2(inc_1_out_2), .ZF(inc_1_zf[8]), .BAF(inc_1_zf[9]), .BOF(inc_1_zf[10]));
  DEC dec_1 (.X(X), .out_2(dec_1_out_2), .ZF(dec_1_zf[8]), .out_4(dec_1_zf[9]), .BOF(dec_1_zf[10]));
  CMPZ cmpz_1 (.X(X), .ZF(cmpz_1_zf[8]), .BOF(cmpz_1_zf[9]));
  INV inv_1 (.X(X), .Z(inv_1_z), .ZF(inv_1_zf[8]), .BAF(inv_1_zf[9]), .BOF(inv_1_zf[10]));
  SHL shl_1 (.X(X), .Z(shl_1_z), .ZF(shl_1_zf[8]), .BOF(shl_1_zf[10]));
  SHR shr_1 (.X(X), .Z(shr_1_z), .ZF(shr_1_zf[8]), .BOF(shr_1_zf[10]));
  ROL rol_1 (.X(X), .Z(rol_1_z), .ZF(rol_1_zf[8]), .BOF(rol_1_zf[10]));
  ROR ror_1 (.in_1(X), .Z(ror_1_z), .ZF(ror_1_zf[8]), .BOF(ror_1_zf[10]));
  NOT not_1 (.X(X), .Z(not_1_z), .ZF(not_1_zf[8]), .BOF(not_1_zf[10]));
  N1 n1_1 (.X(X), .out_2(n1_1_out_2), .ZF(n1_1_zf[8]), .BAF(n1_1_zf[9]), .BOF(n1_1_zf[10]));
  N0 n0_1 (.X(X), .out_2(n0_1_out_2), .ZF(n0_1_zf[8]), .BAF(n0_1_zf[9]), .BOF(n0_1_zf[10]));
  ADD add_1 (.x(X), .y(Y), .Z(add_1_z), .ZF(add_1_zf[8]), .BAF(add_1_zf[9]), .BOF(add_1_zf[10]));
  SUB sub_1 (.X(X), .Y(Y), .Z(sub_1_z), .ZF(sub_1_zf[8]), .BAF(sub_1_zf[9]), .BOF(sub_1_zf[10]));
  MUL mul_1 (.x(X), .y(Y), .Z(mul_1_z), .BAF(mul_1_baf[8]), .ZF(mul_1_baf[9]), .BOF(mul_1_baf[10]));
  DIV div_1 (.X(Y), .Y(Y), .Z(div_1_z), .ZF(div_1_zf[8]), .BAF(div_1_zf[9]), .BOF(div_1_zf[10]));
  XOR xor_1 (.X(Y), .Y(Y), .Z(xor_1_z), .ZF(xor_1_zf[8]), .BOF(xor_1_zf[10]));
  AND and_1 (.X(Y), .Y(Y), .Z(and_1_z), .ZF(and_1_zf[8]), .BOF(and_1_zf[10]));
  OR or_1 (.X(Y), .Y(Y), .Z(or_1_z), .ZF(or_1_zf[8]), .BOF(or_1_zf[10]));
  OP1 op1_1 (.in_1(Y), .in_2(Y), .out_3(op1_1_out_3), .ZF(op1_1_zf[8]), .BAF(op1_1_zf[9]), .BOF(op1_1_zf[10]));
  OP2 op2_1 (.in_1(Y), .in_2(Y), .out_3(op2_1_out_3), .ZF(op2_1_zf[8]), .BAF(op2_1_zf[9]), .BOF(op2_1_zf[10]));
  OP3 op3_1 (.in_1(Y), .Z(op3_1_z), .ZF(op3_1_zf[8]), .BAF(op3_1_zf[9]), .BOF(op3_1_zf[10]));
  Multiplexer #(.select(5), .width(11)) multiplexer_1 (
    .in0(11'h200), .in1({vld_1_zf, vld_1_z}), .in2({neg_1_baf, neg_1_out_2}), .in3({inc_1_zf, inc_1_out_2}),
    .in4({dec_1_zf, dec_1_out_2}), .in5({1'b0, cmpz_1_zf, {8{1'b0}}}), .in6({inv_1_zf, inv_1_z}),
    .in7(11'h200), .in8({{2{shl_1_zf[10]}}, shl_1_zf[8], shl_1_z}),
    .in9({{2{shr_1_zf[10]}}, shr_1_zf[8], shr_1_z}), .in10({{2{rol_1_zf[10]}}, rol_1_zf[8], rol_1_z}),
    .in11({{2{ror_1_zf[10]}}, ror_1_zf[8], ror_1_z}), .in12({{2{not_1_zf[10]}}, not_1_zf[8], not_1_z}),
    .in13({n1_1_zf, n1_1_out_2}), .in14({n0_1_zf, n0_1_out_2}), .in15(11'h200), .in16({add_1_zf, add_1_z}),
    .in17({sub_1_zf, sub_1_z}), .in18({mul_1_baf, mul_1_z}), .in19({div_1_zf, div_1_z}), .in20(11'h200),
    .in21(11'h200), .in22(11'h200), .in23(11'h200), .in24(11'h200), .in25({op1_1_zf, op1_1_out_3}),
    .in26({op2_1_zf, op2_1_out_3}), .in27({op3_1_zf, op3_1_z}), .in28(11'h200),
    .in29({{2{xor_1_zf[10]}}, xor_1_zf[8], xor_1_z}), .in30({{2{and_1_zf[10]}}, and_1_zf[8], and_1_z}),
    .in31({{2{or_1_zf[10]}}, or_1_zf[8], or_1_z}), .out({BOF, BAF, ZF, Z}), .sel(in_1[4:0]));  // open: en

  // Other names for the same wires on the sheet: OPCODE[4:0] = in_1[4:0]

  // Notes on the sheet:
  //   00000001 - VLD 00000010 - NEG
  //   00000011 - INC 00000100 - DEC
  //   00000101 - CMPZ 00000110 - INV
  //   00000011 - INC 00000100 - DEC
  //   00001000 - SHL 00001001 - SHR
  //   00001010 - ROL 00001011 - ROR
  //   00001100 - NOT 00001101 - N1 00001110 - N0
  //   00010000 - ADD 00010001 - SUB
  //   00010010 - MUL 00010011 - DIV
  //   01011000 - op1 01011001 - op2 01011010 - op3
endmodule

module ADD (
  input  [7:0] x,
  input  [7:0] y,
  output [7:0] Z,
  output ZF,
  output BAF,
  output BOF
);

  wire vld_1_baf, vld_2_baf;
  wire [7:0] adder_1_out;
  wire [8:8] adder_1_cout, divider_1_rem;

  Adder adder_1 (.a(x), .b(y), .out(adder_1_out), .cin(1'b0), .cout(adder_1_cout[8]));
  VLD vld_1 (.X(x), .BAF(vld_1_baf));  // open: Z, ZF, BOF
  VLD vld_2 (.X(y), .BAF(vld_2_baf));  // open: Z, ZF, BOF
  Divider #(.width(9)) divider_1 (
    .a({adder_1_cout[8], adder_1_out}), .b(9'h97), .upper({9{1'b0}}), .rem({divider_1_rem[8], Z}));  // open: out
  or or_1 (BAF, vld_1_baf, vld_2_baf);
  CMPZ cmpz_1 (.X(Z), .ZF(ZF));  // open: BOF

  assign BOF = 1'b0;
endmodule

module VLD (
  input  [7:0] X,
  output [7:0] Z,
  output ZF,
  output BAF,
  output BOF
);

  Comparator #(.mode("unsigned")) comparator_1 (.a(X), .b(8'h97), .lt(Z[0]));  // open: gt, eq
  not not_1 (BAF, Z[0]);
  not not_2 (ZF, 1'b1);
  not not_3 (BOF, 1'b1);

  assign Z[7:1] = {7{1'b0}};
endmodule

module NEG (
  input  [7:0] X,
  output [7:0] out_2,
  output BAF,
  output ZF,
  output BOF
);

  wire [7:0] subtractor_1_out;

  Subtractor subtractor_1 (.a(8'h97), .b(X), .out(subtractor_1_out), .bout(BAF));  // open: bin
  Divider divider_1 (.a(subtractor_1_out), .b(8'h97), .rem(out_2));  // open: out, upper
  CMPZ cmpz_1 (.X(out_2), .ZF(ZF));  // open: BOF

  assign BOF = 1'b0;
endmodule

module INC (
  input  [7:0] X,
  output [7:0] out_2,
  output ZF,
  output BAF,
  output BOF
);

  wire [7:0] add_1_z;

  ADD add_1 (.x(X), .y(8'h1), .Z(add_1_z));  // open: ZF, BAF, BOF
  VLD vld_1 (.X(X), .BAF(BAF));  // open: Z, ZF, BOF
  Divider divider_1 (.a(add_1_z), .b(8'h97), .rem(out_2));  // open: out, upper
  CMPZ cmpz_1 (.X(out_2), .ZF(ZF));  // open: BOF

  assign BOF = 1'b0;
endmodule

module DEC (
  input  [7:0] X,
  output [7:0] out_2,
  output ZF,
  output out_4,
  output BOF
);

  wire [7:0] sub_1_z;

  SUB sub_1 (.X(X), .Y(8'h1), .Z(sub_1_z));  // open: ZF, BAF, BOF
  VLD vld_1 (.X(X), .BAF(out_4));  // open: Z, ZF, BOF
  Divider divider_1 (.a(sub_1_z), .b(8'h97), .rem(out_2));  // open: out, upper
  CMPZ cmpz_1 (.X(out_2), .ZF(ZF));  // open: BOF

  assign BOF = 1'b0;
endmodule

module CMPZ (
  input  [7:0] X,
  output ZF,
  output BOF
);

  wire or_1_out;

  or or_1 (or_1_out, X[0], X[1], X[2], X[3], X[4], X[5], X[6], X[7]);
  not not_1 (ZF, or_1_out);

  assign BOF = 1'b0;
endmodule

module MUL (
  input  [7:0] x,
  input  [7:0] y,
  output [7:0] Z,
  output BAF,
  output ZF,
  output BOF
);

  wire vld_1_baf, vld_2_baf;
  wire [7:0] multiplier_1_out;
  wire [15:8] divider_1_rem;

  VLD vld_1 (.X(x), .BAF(vld_1_baf));  // open: Z, ZF, BOF
  VLD vld_2 (.X(y), .BAF(vld_2_baf));  // open: Z, ZF, BOF
  Multiplier multiplier_1 (.a(x), .b(y), .out(multiplier_1_out));  // open: cin, cout
  or or_1 (BAF, vld_1_baf, vld_2_baf);
  Divider #(.width(16)) divider_1 (
    .a({{8{1'b0}}, multiplier_1_out}), .b(16'h97), .rem({divider_1_rem, Z}));  // open: out, upper
  CMPZ cmpz_1 (.X(Z), .ZF(ZF));  // open: BOF

  assign BOF = 1'b0;
endmodule

module DIV (
  input  [7:0] X,
  input  [7:0] Y,
  output [7:0] Z,
  output ZF,
  output BAF,
  output BOF
);

  wire inv_1_baf, vld_1_p3, vld_2_p2;
  wire [7:0] CARRYIN, inv_1_z, multiplier_1_out;

  // VLD vld_1: pin names not known; wires that end beside it: Y, X, vld_1_p3
  // VLD vld_2: pin names not known; wires that end beside it: X, vld_2_p2
  INV inv_1 (.X(Y), .Z(inv_1_z), .BAF(inv_1_baf));  // open: ZF, BOF
  Multiplier multiplier_1 (.a(X), .b(inv_1_z), .out(multiplier_1_out), .cout(CARRYIN));  // open: cin
  or or_1 (BAF, vld_1_p3, inv_1_baf, vld_2_p2);
  Divider divider_1 (.a(multiplier_1_out), .b(8'h97), .upper(CARRYIN), .rem(Z));  // open: out
  CMPZ cmpz_1 (.X(Z), .ZF(ZF));  // open: BOF

  assign BOF = 1'b0;
endmodule

module INV (
  input  [7:0] X,
  output [7:0] Z,
  output ZF,
  output BAF,
  output BOF
);

  wire CMPZ_2_zf, vld_1_p2;

  CMPZ CMPZ (.X(Z), .ZF(ZF));  // open: BOF
  // VLD vld_1: pin names not known; wires that end beside it: X, vld_1_p2
  ROM rom_1 (.addr(X), .data(Z));  // open: sel
  CMPZ CMPZ_2 (.X(Z), .ZF(CMPZ_2_zf));  // open: BOF
  or or_1 (BAF, CMPZ_2_zf, vld_1_p2);

  assign BOF = 1'b0;

  // Notes on the sheet:
  //   contents of rom_1 (hex, n*v repeats v):
  //   0 1 4c 65 26 79 7e 6c 13 54 88 37 3f 5d 36 8d 55 50 2a 8 44 24 67 2e 6b 91 7a 1c 1b 7d 92 27 76 77
  //   28 52 15 31 4 1f 22 46 12 90 7f 2f 17 2d 81 25 94 4d 3d 39 e b 59 35 8a 40 49 34 5f c 3b 4f 87 8e 14
  //   74 29 86 56 3c 64 95 2 33 5b 41 11 6e 23 83 9 10 48 5c 8b 38 63 4e 57 d 62 3e 8c 89 5e 5a 4a 3 72 16
  //   6a 80 68 18 7 85 51 75 78 93 66 82 45 6f 20 21 70 5 1a 7c 7b 1d 6 2c 69 30 73 53 8f 6d 47 42 a 61 3a
  //   58 60 f 43 84 2b 19 1e 71 32 4b 96
endmodule

module SUB (
  input  [7:0] X,
  input  [7:0] Y,
  output [7:0] Z,
  output ZF,
  output BAF,
  output BOF
);

  wire vld_1_baf, vld_2_baf;
  wire [7:0] adder_1_out;
  wire [8:0] subtractor_1_out;
  wire [8:8] adder_1_cout, divider_1_rem;

  Adder adder_1 (.a(X), .b(8'h97), .out(adder_1_out), .cin(1'b0), .cout(adder_1_cout[8]));
  VLD vld_1 (.X(X), .BAF(vld_1_baf));  // open: Z, ZF, BOF
  VLD vld_2 (.X(Y), .BAF(vld_2_baf));  // open: Z, ZF, BOF
  Subtractor #(.width(9)) subtractor_1 (
    .a({adder_1_cout[8], adder_1_out}), .b({1'b0, Y}), .out(subtractor_1_out));  // open: bin, bout
  or or_1 (BAF, vld_1_baf, vld_2_baf);
  Divider #(.width(9)) divider_1 (
    .a(subtractor_1_out), .b(9'h97), .upper({9{1'b0}}), .rem({divider_1_rem[8], Z}));  // open: out
  CMPZ cmpz_1 (.X(Z), .ZF(ZF));  // open: BOF

  assign BOF = 1'b0;
endmodule

module SHL (
  input  [7:0] X,
  output [7:0] Z,
  output ZF,
  output BOF
);

  Shifter shifter_1 (.in(X), .\dist (3'b001), .out(Z));
  CMPZ cmpz_1 (.X(Z), .ZF(ZF));  // open: BOF

  assign BOF = 1'b0;
endmodule

module SHR (
  input  [7:0] X,
  output [7:0] Z,
  output ZF,
  output BOF
);

  Shifter #(.shift("lr")) shifter_1 (.in(X), .\dist (3'b001), .out(Z));
  CMPZ cmpz_1 (.X(Z), .ZF(ZF));  // open: BOF

  assign BOF = 1'b0;
endmodule

module ROL (
  input  [7:0] X,
  output [7:0] Z,
  output ZF,
  output BOF
);

  Shifter #(.shift("rl")) shifter_1 (.in(X), .\dist (3'b001), .out(Z));
  CMPZ cmpz_1 (.X(Z), .ZF(ZF));  // open: BOF

  assign BOF = 1'b0;
endmodule

module ROR (
  input  [7:0] in_1,
  output [7:0] Z,
  output ZF,
  output BOF
);

  Shifter #(.shift("rr")) shifter_1 (.in(in_1), .\dist (3'b001), .out(Z));
  CMPZ cmpz_1 (.X(Z), .ZF(ZF));  // open: BOF

  assign BOF = 1'b0;
endmodule

module XOR (
  input  [7:0] X,
  input  [7:0] Y,
  output [7:0] Z,
  output ZF,
  output BOF
);

  assign Z = X ^ Y;  // XOR_Gate xor_1, 8 bits wide
  CMPZ cmpz_1 (.X(Z), .ZF(ZF));  // open: BOF

  assign BOF = 1'b0;
endmodule

module AND (
  input  [7:0] X,
  input  [7:0] Y,
  output [7:0] Z,
  output ZF,
  output BOF
);

  assign Z = X & Y;  // AND_Gate and_1, 8 bits wide
  CMPZ cmpz_1 (.X(Z), .ZF(ZF));  // open: BOF

  assign BOF = 1'b0;
endmodule

module OR (
  input  [7:0] X,
  input  [7:0] Y,
  output [7:0] Z,
  output ZF,
  output BOF
);

  assign Z = X | Y;  // OR_Gate or_1, 8 bits wide
  CMPZ cmpz_1 (.X(Z), .ZF(ZF));  // open: BOF

  assign BOF = 1'b0;
endmodule

module NOT (
  input  [7:0] X,
  output [7:0] Z,
  output ZF,
  output BOF
);

  assign Z = ~X;  // NOT_Gate not_1, 8 bits wide
  CMPZ cmpz_1 (.X(Z), .ZF(ZF));  // open: BOF

  assign BOF = 1'b0;
endmodule

module N1 (
  input  [7:0] X,
  output [7:0] out_2,
  output ZF,
  output BAF,
  output BOF
);

  wire cmpz_2_zf, cmpz_3_zf, not_1_out;

  ROM rom_1 (.addr(X), .data(out_2));  // open: sel
  CMPZ cmpz_1 (.X(out_2), .ZF(ZF));  // open: BOF
  CMPZ cmpz_2 (.X(out_2), .ZF(cmpz_2_zf));  // open: BOF
  CMPZ cmpz_3 (.X(X), .ZF(cmpz_3_zf));  // open: BOF
  not not_1 (not_1_out, cmpz_3_zf);
  and and_1 (BAF, cmpz_2_zf, not_1_out);

  assign BOF = 1'b0;

  // Notes on the sheet:
  //   contents of rom_1 (hex, n*v repeats v):
  //   0 1 1 2 1 2 2 3 1 2 2 3 2 3 3 4 1 2 2 3 2 3 3 4 2 3 3 4 3 4 4 5 1 2 2 3 2 3 3 4 2 3 3 4 3 4 4 5 2 3
  //   3 4 3 4 4 5 3 4 4 5 4 5 5 6 1 2 2 3 2 3 3 4 2 3 3 4 3 4 4 5 2 3 3 4 3 4 4 5 3 4 4 5 4 5 5 6 2 3 3 4
  //   3 4 4 5 3 4 4 5 4 5 5 6 3 4 4 5 4 5 5 6 4 5 5 6 5 6 6 7 1 2 2 3 2 3 3 4 2 3 3 4 3 4 4 5 2 3 3 4 3 4
  //   4
endmodule

module N0 (
  input  [7:0] X,
  output [7:0] out_2,
  output ZF,
  output BAF,
  output BOF
);

  wire cmpz_2_zf, cmpz_3_zf, not_1_out;

  ROM rom_1 (.addr(X), .data(out_2));  // open: sel
  CMPZ cmpz_1 (.X(out_2), .ZF(ZF));  // open: BOF
  CMPZ cmpz_2 (.X(out_2), .ZF(cmpz_2_zf));  // open: BOF
  CMPZ cmpz_3 (.X(X), .ZF(cmpz_3_zf));  // open: BOF
  not not_1 (not_1_out, cmpz_3_zf);
  and and_1 (BAF, cmpz_2_zf, not_1_out);

  assign BOF = 1'b0;

  // Notes on the sheet:
  //   contents of rom_1 (hex, n*v repeats v):
  //   0 0 1 0 2 1 1 0 3 2 2 1 2 1 1 0 4 3 3 2 3 2 2 1 3 2 2 1 2 1 1 0 5 4 4 3 4 3 3 2 4 3 3 2 3 2 2 1 4 3
  //   3 2 3 2 2 1 3 2 2 1 2 1 1 0 6 5 5 4 5 4 4 3 5 4 4 3 4 3 3 2 5 4 4 3 4 3 3 2 4 3 3 2 3 2 2 1 5 4 4 3
  //   4 3 3 2 4 3 3 2 3 2 2 1 4 3 3 2 3 2 2 1 3 2 2 1 2 1 1 0 7 6 6 5 6 5 5 4 6 5 5 4 5 4 4 3 6 5 5 4 5 4
  //   4
endmodule

module OP1 (
  input  [7:0] in_1,
  input  [7:0] in_2,
  output [7:0] out_3,
  output ZF,
  output BAF,
  output BOF
);

  wire vld_1_baf, vld_2_baf;

  VLD vld_1 (.X(in_1), .BAF(vld_1_baf));  // open: Z, ZF, BOF
  VLD vld_2 (.X(in_2), .BAF(vld_2_baf));  // open: Z, ZF, BOF
  Comparator #(.mode("unsigned")) comparator_1 (.a(in_1), .b(in_2), .gt(out_3[0]));  // open: eq, lt
  or or_1 (BAF, vld_1_baf, vld_2_baf);
  CMPZ cmpz_1 (.X({{7{1'b0}}, out_3[0]}), .ZF(ZF));  // open: BOF

  assign BOF = 1'b0;
  assign out_3[7:1] = {7{1'b0}};
endmodule

module OP2 (
  input  [7:0] in_1,
  input  [7:0] in_2,
  output [7:0] out_3,
  output ZF,
  output BAF,
  output BOF
);

  wire inv_1_baf, vld_1_baf, vld_2_baf;
  wire [7:0] inv_1_z;

  INV inv_1 (.X(in_2), .Z(inv_1_z), .BAF(inv_1_baf));  // open: ZF, BOF
  VLD vld_1 (.X(in_1), .BAF(vld_1_baf));  // open: Z, ZF, BOF
  VLD vld_2 (.X(in_2), .BAF(vld_2_baf));  // open: Z, ZF, BOF
  Comparator #(.mode("unsigned")) comparator_1 (.a(in_1), .b(inv_1_z), .eq(out_3[0]));  // open: gt, lt
  or or_1 (BAF, vld_1_baf, inv_1_baf, vld_2_baf);
  CMPZ cmpz_1 (.X({{7{1'b0}}, out_3[0]}), .ZF(ZF));  // open: BOF

  assign BOF = 1'b0;
  assign out_3[7:1] = {7{1'b0}};
endmodule

module OP3 (
  input  [7:0] in_1,
  output [7:0] Z,
  output ZF,
  output BAF,
  output BOF
);

  wire cmpz_1_zf, not_1_out;

  ROM rom_1 (.addr(in_1), .data(Z));  // open: sel
  CMPZ cmpz_1 (.X(in_1), .ZF(cmpz_1_zf));  // open: BOF
  CMPZ cmpz_2 (.X(Z), .ZF(ZF));  // open: BOF
  not not_1 (not_1_out, cmpz_1_zf);
  and and_1 (BAF, ZF, not_1_out);

  assign BOF = 1'b0;

  // Notes on the sheet:
  //   contents of rom_1 (hex, n*v repeats v):
  //   0 1 10 51 69 15 58 88 13 44 22 91 31 16 3e 28 2 12 1f 8 5b 90 37 26 1d 8b 32 48 56 94 24 5 20 76 89
  //   8a 2b 64 80 79 61 62 27 a 7d 45 4 74 b 4a 6e 63 2d 7f 5f 19 11 2c 67 40 7b 2f 50 25 3b 9 4c 14 4e 3a
  //   5e 2a 54 7c 5a 55 55 5a 7c 54 2a 5e 3a 4e 14 4c 9 3b 25 50 2f 7b 40 67 2c 11 19 5f 7f 2d 63 6e 4a b
  //   74 4 45 7d a 27 62 61 79 80 64 2b 8a 89 76 20 5 24 94 56 48 32 8b 1d 26 37 90 5b 8 1f 12 2 28 3e 16
  //   31 91 22 44 13 88 58 15 69 51 10 1
endmodule
