// Logisim project labdarbad.circ as structural Verilog
module ALU (
  input  [7:0] x,
  input  [7:0] y
);

  ADD add_1 ();  // open: x, y, Z, BAF
  Multiplexer #(.select(5), .width(32)) multiplexer_1 ();  // open: in0, in1, in2, in3, in4, in5, in6, in7, in8, in9, in10, in11, in12, in13, in14, in15, in16, in17, in18, in19, in20, in21, in22, in23, in24, in25, in26, in27, in28, in29, in30, in31, out, sel, en
endmodule

module ADD (
  input  [7:0] x,
  input  [7:0] y,
  output [7:0] Z,
  output BAF
);

  wire vld_1_bof, vld_2_bof;
  wire [7:0] adder_1_out;
  wire [8:8] adder_1_cout, divider_1_rem;

  Adder adder_1 (.a(x), .b(y), .out(adder_1_out), .cin(1'b0), .cout(adder_1_cout[8]));
  VLD vld_1 (.in_1(x), .BOF(vld_1_bof));  // open: Z
  VLD vld_2 (.in_1(y), .BOF(vld_2_bof));  // open: Z
  Divider #(.width(9)) divider_1 (
    .a({adder_1_cout[8], adder_1_out}), .b(9'h97), .upper({9{1'b0}}), .rem({divider_1_rem[8], Z}));  // open: out
  or or_1 (BAF, vld_1_bof, vld_2_bof);
endmodule

module VLD (
  input  [7:0] in_1,
  output Z,
  output BOF
);

  Comparator #(.mode("unsigned")) comparator_1 (.a(in_1), .b(8'h97), .lt(Z));  // open: gt, eq
  not not_1 (BOF, Z);
endmodule

module NEG (
  input  [7:0] in_1,
  output [7:0] out_2,
  output BAF
);

  wire [7:0] subtractor_1_out;

  Subtractor subtractor_1 (.a(8'h97), .b(in_1), .out(subtractor_1_out), .bout(BAF));  // open: bin
  Divider divider_1 (.a(subtractor_1_out), .b(8'h97), .rem(out_2));  // open: out, upper
endmodule

module INC (
  input  [7:0] in_1,
  output [7:0] out_2,
  output out_3
);

  wire [7:0] add_1_z;

  ADD add_1 (.x(in_1), .y(8'h1), .Z(add_1_z));  // open: BAF
  VLD vld_1 (.in_1(in_1), .BOF(out_3));  // open: Z
  Divider divider_1 (.a(add_1_z), .b(8'h97), .rem(out_2));  // open: out, upper
endmodule

module DEC (
  input  [7:0] in_1,
  output [7:0] out_2,
  output out_3
);

  wire [7:0] add_1_z;

  ADD add_1 (.x(in_1), .y({8{1'b0}}), .Z(add_1_z));  // open: BAF
  VLD vld_1 (.in_1(in_1), .BOF(out_3));  // open: Z
  Divider divider_1 (.a(add_1_z), .b(8'h97), .rem(out_2));  // open: out, upper
endmodule

module CMPZ (
  input  [7:0] in_1,
  output [7:0] out_2
);

  wire and_1_out;

  and and_1 (and_1_out, in_1[0], in_1[1], in_1[2], in_1[3], in_1[4], in_1[5], in_1[6], in_1[7]);
  not not_1 (out_2[0], and_1_out);
endmodule
